// Logisim project 01-09.circ as structural Verilog: 1 circuit, main circuit main
module main (
  input  I3,
  input  I2,
  input  I1,
  input  I0,
  output S1,
  output S0
);

  wire not_1_out, not_2_out;

  not not_1 (not_1_out, I1);
  not not_2 (not_2_out, I2);
  and and_1 (S0, not_1_out, I0);
  and and_2 (S1, not_2_out, I1, I0);

  // Notes on the sheet:
  //   BCD a AIKEN
endmodule
