// Logisim project 2DMem4bits.circ as structural Verilog: 1 circuit, main circuit main
module main (
  input  in_1,
  input  in_2,
  input  Imput,
  input  W,
  input  L,
  output out_6
);

  wire and_1_out, and_2_out, and_3_out, and_4_out, main_1_o, main_2_o, main_3_o, main_4_o, not_1_out,
       not_2_out, or_1_out;

  _2DMemPoint_main main_1 (.W(W), .I(Imput), .S(and_1_out), .O(main_1_o));
  _2DMemPoint_main main_2 (.W(W), .I(Imput), .S(and_3_out), .O(main_2_o));
  _2DMemPoint_main main_3 (.W(W), .I(Imput), .S(and_2_out), .O(main_3_o));
  _2DMemPoint_main main_4 (.W(W), .I(Imput), .S(and_4_out), .O(main_4_o));
  or or_1 (or_1_out, main_2_o, main_1_o, main_3_o, main_4_o);
  not not_1 (not_1_out, in_1);
  and and_1 (and_1_out, not_1_out, not_2_out);
  and and_2 (and_2_out, not_1_out, in_2);
  and and_3 (and_3_out, not_2_out, in_1);
  and and_4 (and_4_out, in_1, in_2);
  and and_5 (out_6, or_1_out, L);
  not not_2 (not_2_out, in_2);
endmodule
