// Logisim project 2DMemPoint.circ as structural Verilog: 1 circuit, main circuit main
module main (
  input  S,
  input  W,
  input  I,
  output O
);

  wire and_1_out, and_2_out, clock_1_out, j_k_ff_1_q, not_1_out;

  not not_1 (not_1_out, I);
  and and_1 (and_1_out, W, S, I);
  and and_2 (and_2_out, W, S, not_1_out);
  J_K_Flip_Flop j_k_ff_1 (
    .J(and_1_out), .clk(clock_1_out), .K(and_2_out), .Q(j_k_ff_1_q));  // open: Qn, preset, en, reset
  Clock clock_1 (.out(clock_1_out));
  and and_3 (O, S, j_k_ff_1_q);
endmodule
