// Logisim project 4ParalelAdder.circ as structural Verilog: 1 circuit, main circuit main
module main (
  input  A2,
  input  A3,
  input  A1,
  input  A0,
  input  B3,
  input  B2,
  input  B1,
  input  B0,
  output CarryO,
  output S3,
  output S2,
  output S1,
  output S0
);

  wire main_2_cyout, main_3_cyout, main_4_cy;

  Adder_main main_1 (.in_1(B3), .in_2(A3), .Cy(main_2_cyout), .O(S3), .CyOut(CarryO));
  Adder_main main_2 (.in_1(A2), .in_2(B2), .Cy(main_3_cyout), .O(S2), .CyOut(main_2_cyout));
  Adder_main main_3 (.in_1(A1), .in_2(B1), .Cy(main_4_cy), .O(S1), .CyOut(main_3_cyout));
  HalfAdder_main main_4 (.A(A0), .B(B0), .O(S0), .Cy(main_4_cy));
endmodule
