// Logisim project 4Paralelsubstractor.circ as structural Verilog: 1 circuit, main circuit main
module main (
  input  A3,
  input  B3,
  input  A2,
  input  B2,
  input  A1,
  input  B1,
  input  A0,
  input  B0,
  output out_9,
  output out_10,
  output out_11,
  output out_12,
  output out_13
);

  wire main_2_cyout, main_3_cyout, main_4_cy;

  Substractor_main main_1 (.in_1(A3), .in_2(B3), .Cy(main_2_cyout), .O(out_10), .CyOut(out_9));
  Substractor_main main_2 (.in_1(A2), .in_2(B2), .Cy(main_3_cyout), .O(out_11), .CyOut(main_2_cyout));
  Substractor_main main_3 (.in_1(A1), .in_2(B1), .Cy(main_4_cy), .O(out_12), .CyOut(main_3_cyout));
  HalfSubstractor_main main_4 (.A(A0), .B(B0), .S(out_13), .Cy(main_4_cy));
endmodule
