// Logisim project ALUEj.circ as structural Verilog: 1 circuit, main circuit main
module main (
  input  Op1,
  input  Op2
);

  wire A0_q, A0_qn, A1_q, A1_qn, A2_q, A2_qn, and_1_out, and_2_out, and_3_out, and_4_out, and_11_out,
       and_12_out, and_13_out, and_14_out, and_15_out, and_16_out, and_17_out, and_18_out, and_19_out,
       and_20_out, and_21_out, and_22_out, B0_q, B0_qn, B1_q, B1_qn, B2_q, B2_qn, clock_1_out, not_1_out,
       not_2_out, not_3_out, not_4_out, not_5_out, not_6_out, not_7_out, or_1_out, or_2_out, or_3_out,
       or_4_out, or_5_out, or_6_out, xor_1_out, xor_2_out, xor_3_out;
  wire [2:0] and_5_out, and_6_out;

  Clock clock_1 (.out(clock_1_out));
  not not_1 (not_1_out, Op2);
  not not_2 (not_2_out, Op2);
  not not_3 (not_3_out, Op1);
  and and_1 (and_1_out, not_1_out, Op1);
  and and_2 (and_2_out, not_2_out, not_3_out);
  not not_4 (not_4_out, Op1);
  and and_3 (and_3_out, Op2, not_4_out);
  and and_4 (and_4_out, Op2, Op1);
  D_Flip_Flop B0 (.clk(clock_1_out), .Q(B0_q), .Qn(B0_qn));  // open: D, preset, en, reset
  D_Flip_Flop B1 (.clk(clock_1_out), .Q(B1_q), .Qn(B1_qn));  // open: D, preset, en, reset
  D_Flip_Flop B2 (.clk(clock_1_out), .Q(B2_q), .Qn(B2_qn));  // open: D, preset, en, reset
  and and_5 (and_5_out[0], and_2_out, B0_q);
  and and_6 (and_6_out[0], and_2_out, B0_qn);
  and and_7 (and_5_out[1], and_2_out, B1_q);
  and and_8 (and_6_out[1], and_2_out, B1_qn);
  and and_9 (and_5_out[2], and_2_out, B2_q);
  and and_10 (and_6_out[2], and_2_out, B2_qn);
  xor xor_1 (xor_1_out, B0_q, A0_q);
  buf xor_2 (xor_2_out, B1_q);  // XOR_Gate
  buf xor_3 (xor_3_out, B2_q);  // XOR_Gate
  and and_11 (and_11_out, xor_1_out, and_3_out);
  and and_12 (and_12_out, and_3_out, not_5_out);
  not not_5 (not_5_out, xor_1_out);
  and and_13 (and_13_out, and_3_out, not_6_out);
  and and_14 (and_14_out, xor_2_out, and_3_out);
  not not_6 (not_6_out, xor_2_out);
  and and_15 (and_15_out, and_3_out, not_7_out);
  and and_16 (and_16_out, xor_3_out, and_3_out);
  not not_7 (not_7_out, xor_3_out);
  or or_1 (or_1_out, and_4_out, and_6_out[0], and_17_out, and_11_out);
  or or_2 (or_2_out, and_19_out, and_5_out[0], and_12_out);
  or or_3 (or_3_out, and_4_out, and_6_out[1], and_14_out, and_18_out);
  or or_4 (or_4_out, and_5_out[1], and_20_out, and_13_out);
  or or_5 (or_5_out, and_4_out, and_6_out[2], and_16_out, and_22_out);
  or or_6 (or_6_out, and_5_out[2], and_15_out, and_21_out);
  J_K_Flip_Flop A0 (.J(or_1_out), .clk(clock_1_out), .K(or_2_out), .Q(A0_q), .Qn(A0_qn));  // open: preset, en, reset
  and and_17 (and_17_out, A1_q, and_1_out);
  J_K_Flip_Flop A1 (.J(or_3_out), .clk(clock_1_out), .K(or_4_out), .Q(A1_q), .Qn(A1_qn));  // open: preset, en, reset
  and and_18 (and_18_out, A2_q, and_1_out);
  J_K_Flip_Flop A2 (.J(or_5_out), .clk(clock_1_out), .K(or_6_out), .Q(A2_q), .Qn(A2_qn));  // open: preset, en, reset
  and and_19 (and_19_out, A1_qn, and_1_out);
  and and_20 (and_20_out, A2_qn, and_1_out);
  and and_21 (and_21_out, and_1_out, A0_qn);
  and and_22 (and_22_out, A0_q, and_1_out);
endmodule
