// Logisim project Alu_Completo.circ as structural Verilog: 1 circuit, main circuit main
module main (
  input  in_1,
  input  in_2,
  input  in_3,
  output out_4,
  output out_5,
  output out_6,
  output out_7,
  output out_8,
  output out_9,
  output out_10,
  output out_11,
  output out_12,
  output out_13
);

  wire adder_2_cout, adder_3_cout, adder_4_cout, and_2_out, and_3_out, and_4_out, and_5_out, and_6_out,
       and_7_out, and_8_out, and_9_out, and_10_out, and_11_out, and_12_out, and_13_out, and_14_out,
       and_15_out, and_16_out, and_17_out, and_18_out, and_19_out, and_20_out, and_21_out, and_22_out,
       and_23_out, and_24_out, and_25_out, and_26_out, and_27_out, and_28_out, and_29_out, and_30_out,
       and_31_out, and_32_out, and_33_out, and_34_out, and_35_out, and_36_out, and_37_out, and_38_out,
       and_39_out, and_40_out, clock_1_out, j_k_ff_1_q, j_k_ff_1_qn, j_k_ff_2_q, j_k_ff_2_qn, j_k_ff_3_q,
       j_k_ff_3_qn, j_k_ff_4_q, j_k_ff_4_qn, j_k_ff_5_q, j_k_ff_5_qn, j_k_ff_6_q, j_k_ff_6_qn, j_k_ff_7_q,
       j_k_ff_7_qn, j_k_ff_8_q, j_k_ff_8_qn, not_1_out, not_2_out, not_3_out, not_4_out, not_5_out,
       not_6_out, not_7_out, not_8_out, not_9_out, not_10_out, not_11_out, not_12_out, not_13_out,
       not_14_out, not_15_out, not_16_out, or_1_out, or_2_out, or_3_out, or_4_out, or_5_out, or_6_out,
       or_7_out, or_8_out, or_9_out, or_10_out, or_11_out, or_12_out, or_17_out, or_18_out, or_19_out,
       or_20_out, or_21_out, or_22_out, or_23_out, or_24_out, xor_1_out, xor_2_out, xor_3_out, xor_4_out;

  not not_1 (not_1_out, j_k_ff_2_q);
  not not_2 (not_2_out, j_k_ff_3_q);
  not not_3 (not_3_out, j_k_ff_4_q);
  not not_4 (not_4_out, j_k_ff_1_q);
  and and_1 (out_13, and_26_out, j_k_ff_1_qn, j_k_ff_2_qn, j_k_ff_3_qn, j_k_ff_4_qn);
  and and_2 (and_2_out, and_24_out, j_k_ff_2_q);
  and and_3 (and_3_out, and_24_out, not_1_out);
  and and_4 (and_4_out, and_24_out, j_k_ff_3_q);
  and and_5 (and_5_out, and_24_out, not_2_out);
  and and_6 (and_6_out, and_24_out, j_k_ff_4_q);
  and and_7 (and_7_out, and_24_out, not_3_out);
  and and_8 (and_8_out, j_k_ff_1_q, and_24_out);
  and and_9 (and_9_out, not_4_out, and_24_out);
  buf or_1 (or_1_out, and_8_out);  // OR_Gate
  buf or_2 (or_2_out, and_9_out);  // OR_Gate
  and and_10 (and_10_out, and_16_out, or_3_out);
  or or_3 (or_3_out, j_k_ff_1_q, j_k_ff_5_q);
  buf or_4 (or_4_out, and_2_out);  // OR_Gate
  buf or_5 (or_5_out, and_3_out);  // OR_Gate
  buf or_6 (or_6_out, and_4_out);  // OR_Gate
  buf or_7 (or_7_out, and_5_out);  // OR_Gate
  buf or_8 (or_8_out, and_6_out);  // OR_Gate
  buf or_9 (or_9_out, and_7_out);  // OR_Gate
  and and_11 (and_11_out, and_16_out, or_10_out);
  or or_10 (or_10_out, j_k_ff_2_q, j_k_ff_6_q);
  xor xor_1 (xor_1_out, j_k_ff_1_q, j_k_ff_5_q);
  xor xor_2 (xor_2_out, j_k_ff_2_q, j_k_ff_6_q);
  J_K_Flip_Flop j_k_ff_1 (
    .J(or_4_out), .clk(clock_1_out), .K(or_5_out), .Q(j_k_ff_1_q), .Qn(j_k_ff_1_qn));  // open: preset, en, reset
  J_K_Flip_Flop j_k_ff_2 (
    .J(or_6_out), .clk(clock_1_out), .K(or_7_out), .Q(j_k_ff_2_q), .Qn(j_k_ff_2_qn));  // open: preset, en, reset
  J_K_Flip_Flop j_k_ff_3 (
    .J(or_8_out), .clk(clock_1_out), .K(or_9_out), .Q(j_k_ff_3_q), .Qn(j_k_ff_3_qn));  // open: preset, en, reset
  J_K_Flip_Flop j_k_ff_4 (
    .J(or_1_out), .clk(clock_1_out), .K(or_2_out), .Q(j_k_ff_4_q), .Qn(j_k_ff_4_qn));  // open: preset, en, reset
  and and_12 (and_12_out, and_16_out, or_11_out);
  or or_11 (or_11_out, j_k_ff_3_q, j_k_ff_7_q);
  xor xor_3 (xor_3_out, j_k_ff_3_q, j_k_ff_7_q);
  and and_13 (and_13_out, or_12_out, and_16_out);
  or or_12 (or_12_out, j_k_ff_4_q, j_k_ff_8_q);
  and and_14 (and_14_out, xor_1_out, and_33_out);
  xor xor_4 (xor_4_out, j_k_ff_4_q, j_k_ff_8_q);
  and and_15 (and_15_out, and_21_out, j_k_ff_1_q, j_k_ff_5_q);
  and and_16 (and_16_out, in_1, not_6_out, not_7_out);
  and and_17 (and_17_out, xor_2_out, and_33_out);
  or or_13 (out_9, and_14_out, and_10_out, and_15_out);
  or or_14 (out_10, and_17_out, and_18_out, and_11_out);
  and and_18 (and_18_out, and_21_out, j_k_ff_2_q, j_k_ff_6_q);
  or or_15 (out_11, and_22_out, and_12_out, and_19_out);
  and and_19 (and_19_out, and_21_out, j_k_ff_3_q, j_k_ff_7_q);
  and and_20 (and_20_out, j_k_ff_4_q, and_21_out, j_k_ff_8_q);
  or or_16 (out_12, and_20_out, and_23_out, and_13_out);
  and and_21 (and_21_out, in_1, not_5_out, in_3);
  not not_5 (not_5_out, in_2);
  not not_6 (not_6_out, in_2);
  not not_7 (not_7_out, in_3);
  and and_22 (and_22_out, xor_3_out, and_33_out);
  and and_23 (and_23_out, xor_4_out, and_33_out);
  Clock clock_1 (.out(clock_1_out));
  and and_24 (and_24_out, in_1, in_2, not_8_out);
  not not_8 (not_8_out, in_3);
  not not_9 (not_9_out, in_1);
  and and_25 (and_25_out, not_9_out, in_2, in_2, in_3);
  not not_10 (not_10_out, j_k_ff_5_q);
  not not_11 (not_11_out, j_k_ff_6_q);
  not not_12 (not_12_out, j_k_ff_7_q);
  not not_13 (not_13_out, in_1);
  and and_26 (and_26_out, not_13_out, in_2, not_14_out);
  and and_27 (and_27_out, j_k_ff_5_q, and_34_out);
  and and_28 (and_28_out, not_10_out, and_34_out);
  and and_29 (and_29_out, j_k_ff_6_q, and_34_out);
  and and_30 (and_30_out, not_11_out, and_34_out);
  buf and_31 (and_31_out, j_k_ff_7_q);  // AND_Gate
  buf and_32 (and_32_out, not_12_out);  // AND_Gate
  not not_14 (not_14_out, in_3);
  not not_15 (not_15_out, in_1);
  not not_16 (not_16_out, in_2);
  and and_33 (and_33_out, not_15_out, not_16_out, in_3);
  buf or_17 (or_17_out, and_27_out);  // OR_Gate
  buf or_18 (or_18_out, and_28_out);  // OR_Gate
  buf or_19 (or_19_out, and_29_out);  // OR_Gate
  buf or_20 (or_20_out, and_30_out);  // OR_Gate
  buf or_21 (or_21_out, and_31_out);  // OR_Gate
  buf or_22 (or_22_out, and_32_out);  // OR_Gate
  and and_34 (and_34_out, in_1, in_2, in_3);
  J_K_Flip_Flop j_k_ff_5 (
    .J(or_23_out), .clk(clock_1_out), .K(or_24_out), .Q(j_k_ff_5_q), .Qn(j_k_ff_5_qn));  // open: preset, en, reset
  J_K_Flip_Flop j_k_ff_6 (
    .J(or_17_out), .clk(clock_1_out), .K(or_18_out), .Q(j_k_ff_6_q), .Qn(j_k_ff_6_qn));  // open: preset, en, reset
  J_K_Flip_Flop j_k_ff_7 (
    .J(or_19_out), .clk(clock_1_out), .K(or_20_out), .Q(j_k_ff_7_q), .Qn(j_k_ff_7_qn));  // open: preset, en, reset
  J_K_Flip_Flop j_k_ff_8 (
    .J(or_21_out), .clk(clock_1_out), .K(or_22_out), .Q(j_k_ff_8_q), .Qn(j_k_ff_8_qn));  // open: preset, en, reset
  Adder #(.width(1)) adder_1 (.a(adder_2_cout), .b(and_35_out), .out(out_5), .cout(out_4));  // open: cin
  and and_35 (and_35_out, j_k_ff_5_qn, and_25_out);
  buf and_36 (and_36_out, j_k_ff_8_q);  // AND_Gate
  buf and_37 (and_37_out, j_k_ff_8_qn);  // AND_Gate
  Adder #(.width(1)) adder_2 (.a(adder_3_cout), .b(and_38_out), .out(out_6), .cout(adder_2_cout));  // open: cin
  and and_38 (and_38_out, j_k_ff_6_qn, and_25_out);
  buf or_23 (or_23_out, and_36_out);  // OR_Gate
  buf or_24 (or_24_out, and_37_out);  // OR_Gate
  Adder #(.width(1)) adder_3 (.a(adder_4_cout), .b(and_39_out), .out(out_7), .cout(adder_3_cout));  // open: cin
  and and_39 (and_39_out, j_k_ff_7_qn, and_25_out);
  Adder #(.width(1)) adder_4 (.a(1'b1), .b(and_40_out), .out(out_8), .cout(adder_4_cout));  // open: cin
  and and_40 (and_40_out, j_k_ff_8_qn, and_25_out);
endmodule
