// Logisim project Binary Counter.circ as structural Verilog: 1 circuit, main circuit main
module main (
  input  E,
  input  X,
  output out_3,
  output out_4,
  output Cy
);

  wire and_1_out, and_2_out, not_1_out, not_2_out, not_3_out, not_4_out, xor_1_out;

  J_K_Flip_Flop j_k_ff_1 (.J(E), .clk(E), .K(E), .Q(out_4));  // open: Qn, preset, en, reset
  J_K_Flip_Flop j_k_ff_2 (.J(xor_1_out), .clk(xor_1_out), .K(xor_1_out), .Q(out_3));  // open: Qn, preset, en, reset
  not not_1 (not_1_out, X);
  not not_2 (not_2_out, E);
  xor xor_1 (xor_1_out, out_4, X);
  and and_1 (and_1_out, out_4, out_3, X, E);
  not not_3 (not_3_out, out_4);
  not not_4 (not_4_out, out_3);
  or or_1 (Cy, and_1_out, and_2_out);
  and and_2 (and_2_out, not_3_out, not_4_out, not_1_out, not_2_out);
endmodule
