// Logisim project DAddCorrector.circ as structural Verilog: 1 circuit, main circuit main
module main (
  input  Cy,
  input  S3,
  input  S2,
  input  S1,
  output Z
);

  wire and_1_out, or_2_out;

  and and_1 (and_1_out, S3, or_2_out);
  or or_1 (Z, Cy, and_1_out);
  or or_2 (or_2_out, S2, S1);
endmodule
