// Logisim project Digital Adder.circ as structural Verilog: 1 circuit, main circuit main
module main (
  input  in_1,
  input  in_2,
  input  in_3,
  input  in_4,
  input  B2,
  input  in_6,
  input  in_7,
  input  in_8,
  output out_9,
  output out_10,
  output out_11,
  output out_12,
  output out_13
);

  wire _4Adder_carryo, _4Adder_s1, _4Adder_s2, Det_z, main_1_cyout, main_2_cy;

  Adder_main main_1 (.in_1(_4Adder_s2), .in_2(Det_z), .Cy(main_2_cy), .O(out_10), .CyOut(main_1_cyout));
  or or_1 (out_13, main_1_cyout, _4Adder_carryo);
  HalfAdder_main main_2 (.A(Det_z), .B(_4Adder_s1), .O(out_11), .Cy(main_2_cy));
  DAddCorrector_main Det (.Cy(_4Adder_carryo), .S3(out_9), .S2(_4Adder_s2), .S1(_4Adder_s1), .Z(Det_z));
  _4ParalelAdder_main _4Adder (
    .B3(in_7), .A3(in_6), .B2(B2), .B1(in_4), .A1(in_3), .B0(in_2), .A0(in_1), .A2(in_8),
    .CarryO(_4Adder_carryo), .S3(out_9), .S2(_4Adder_s2), .S1(_4Adder_s1), .S0(out_12));
endmodule
