// Logisim project DistribudorFases.circ as structural Verilog: 1 circuit, main circuit main
module main (
  output out_1,
  output out_2,
  output out_3,
  output out_4
);

  wire clock_1_out;

  Clock clock_1 (.out(clock_1_out));
  and and_1 (out_2, clock_1_out, out_1);
  and and_2 (out_4, clock_1_out, out_3);
  S_R_Flip_Flop #(.trigger("falling")) s_r_ff_1 (
    .S(out_4), .clk(clock_1_out), .R(out_2), .Q(out_1));  // open: Qn, preset, reset, en
  S_R_Flip_Flop #(.trigger("falling")) s_r_ff_2 (
    .S(out_2), .clk(clock_1_out), .R(out_4), .Q(out_3));  // open: Qn, preset, reset, en
endmodule
