// Logisim project HalfAdder.circ as structural Verilog: 1 circuit, main circuit main
module main (
  input  A,
  input  B,
  output O,
  output Cy
);

  xor xor_1 (O, A, B);
  and and_1 (Cy, B, A);
endmodule
