// Logisim project HalfSubstractor.circ as structural Verilog: 1 circuit, main circuit main
module main (
  input  A,
  input  B,
  output S,
  output Cy
);

  wire not_1_out;

  xor xor_1 (S, A, B);
  not not_1 (not_1_out, A);
  and and_1 (Cy, not_1_out, B);
endmodule
