// Logisim project Substractor.circ as structural Verilog: 1 circuit, main circuit main
module main (
  input  in_1,
  input  in_2,
  input  Cy,
  output O,
  output CyOut
);

  wire and_1_out, and_2_out, not_1_out, or_1_out, xor_1_out;

  not not_1 (not_1_out, in_1);
  xor xor_1 (xor_1_out, in_2, Cy);
  or or_1 (or_1_out, not_1_out, in_2);
  xor xor_2 (O, in_1, xor_1_out);
  and and_1 (and_1_out, not_1_out, in_2);
  and and_2 (and_2_out, or_1_out, Cy);
  or or_2 (CyOut, and_1_out, and_2_out);
endmodule
