// Logisim project SumadorCorrQuinario.circ as structural Verilog
module semisum (
  input  X0,
  input  Y0,
  output Cy,
  output S
);

  main main_1 ();
  main main_2 ();
  and and_1 (Cy, Y0, X0);
  xor xor_1 (S, X0, Y0);
endmodule

module sum4bit (
  input  in_1,
  input  in_2,
  input  in_3,
  input  in_4,
  input  in_5,
  input  in_6,
  input  in_7,
  input  in_8,
  input  in_9,
  input  in_10,
  input  in_11,
  input  in_12,
  input  in_13,
  input  in_14,
  output out_15,
  output out_16,
  output out_17,
  output out_18,
  output out_19,
  output out_20,
  output S,
  output Cy,
  output V
);

  wire and_1_out, and_2_out, corrector_1_x, or_2_out, or_3_out, or_4_out, semisum_2_cy, semisum_3_cy,
       semisum_4_cy, semisum_5_cy, semisum_6_cy, semisum_6_s, sum_1_out_5, sum_1_s1, sum_2_out_5, sum_2_s1,
       sum_3_out_5, sum_4_out_5, sum_4_s1, sum_5_out_5, sum_5_s1, sum_6_out_5, sum_6_s1, sum_7_out_5,
       sum_8_out_5, sum_8_s1, xor_2_out;

  xor xor_1 (V, Cy, semisum_2_cy);
  main main_1 ();
  semisum semisum_1 (.Cy(Cy), .S(S), .X0(sum_1_s1), .Y0(semisum_2_cy));
  CORRECTOR corrector_1 (.S3(sum_1_s1), .S2(sum_2_s1), .S1(sum_4_s1), .S0(sum_5_s1), .X(corrector_1_x));
  and and_1 (and_1_out, or_2_out, sum_2_s1);
  // OR_Gate or_1 has open pins: in0=and_1_out, in1=sum_2_out_5, out=open
  SUM sum_1 (.out_5(sum_1_out_5), .S1(sum_1_s1), .X(in_6), .Y1(in_8), .CY(sum_2_out_5));
  semisum semisum_2 (.Cy(semisum_2_cy), .S(out_15), .X0(sum_2_s1), .Y0(sum_3_out_5));
  SUM sum_2 (.out_5(sum_2_out_5), .S1(sum_2_s1), .X(in_1), .Y1(in_9), .CY(sum_4_out_5));
  or or_2 (or_2_out, sum_5_s1, sum_4_s1);
  SUM sum_3 (.out_5(sum_3_out_5), .S1(out_16), .X(corrector_1_x), .Y1(sum_4_s1), .CY(semisum_3_cy));
  SUM sum_4 (.out_5(sum_4_out_5), .S1(sum_4_s1), .X(in_2), .Y1(in_10), .CY(sum_5_out_5));
  semisum semisum_3 (.Cy(semisum_3_cy), .S(out_17), .X0(corrector_1_x), .Y0(sum_5_s1));
  SUM sum_5 (.out_5(sum_5_out_5), .S1(sum_5_s1), .X(in_7), .Y1(in_11), .CY(xor_2_out));
  or or_3 (or_3_out, and_2_out, sum_6_out_5);
  xor xor_2 (xor_2_out, semisum_4_cy, sum_6_out_5);
  and and_2 (and_2_out, or_4_out, sum_6_s1);
  semisum semisum_4 (.Cy(semisum_4_cy), .S(out_18), .X0(sum_6_s1), .Y0(sum_7_out_5));
  or or_4 (or_4_out, semisum_6_s, sum_8_s1);
  SUM sum_6 (.out_5(sum_6_out_5), .S1(sum_6_s1), .X(in_3), .Y1(in_12), .CY(sum_8_out_5));
  SUM sum_7 (.out_5(sum_7_out_5), .S1(out_19), .X(or_3_out), .Y1(sum_8_s1), .CY(semisum_5_cy));
  SUM sum_8 (.out_5(sum_8_out_5), .S1(sum_8_s1), .X(in_4), .Y1(in_13), .CY(semisum_6_cy));
  semisum semisum_5 (.Cy(semisum_5_cy), .S(out_20), .X0(or_3_out), .Y0(semisum_6_s));
  semisum semisum_6 (.Cy(semisum_6_cy), .S(semisum_6_s), .X0(in_5), .Y0(in_14));
endmodule

module SUM (
  input  X,
  input  Y1,
  input  CY,
  output S1,
  output out_5
);

  wire and_1_out, and_2_out, or_2_out, xor_1_out;

  or or_1 (out_5, and_1_out, and_2_out);
  and and_1 (and_1_out, CY, or_2_out);
  and and_2 (and_2_out, X, Y1);
  or or_2 (or_2_out, X, Y1);
  xor xor_1 (xor_1_out, X, Y1);
  xor xor_2 (S1, xor_1_out, CY);
endmodule

module CORRECTOR (
  input  S3,
  input  S2,
  input  S1,
  input  S0,
  output X
);

  wire and_1_out, and_2_out, and_3_out, not_1_out, not_2_out, not_3_out;

  not not_1 (not_1_out, S3);
  and and_1 (and_1_out, not_1_out, S2, S0);
  not not_2 (not_2_out, S3);
  and and_2 (and_2_out, not_2_out, S2, S1);
  and and_3 (and_3_out, S3, not_3_out);
  not not_3 (not_3_out, S2);
  or or_1 (X, and_1_out, and_2_out, and_3_out);
endmodule
