// Logisim project SumadorQuinarioTutoria.circ as structural Verilog: 1 circuit, main circuit main
module main (
  input  in_1,
  input  in_2,
  input  in_3,
  input  in_4,
  input  in_5,
  input  in_6,
  input  in_7,
  input  in_8,
  input  in_9,
  input  in_10,
  input  in_11,
  input  in_12,
  output out_13,
  output out_14,
  output out_15,
  output out_16,
  output out_17,
  output Detector,
  output Detector_2,
  output out_20
);

  wire and_1_out, and_2_out, and_3_out, and_4_out, main_1_cyout, main_2_cyout, main_3_cyout, main_3_o,
       main_4_cy, main_5_cyout, main_5_o, main_6_cyout, main_7_cyout, main_8_cyout, main_8_o, main_9_cy,
       main_10_cy, main_10_o, xor_1_out;

  or or_1 (Detector, main_1_cyout, and_2_out, and_1_out);
  and and_1 (and_1_out, main_5_o, out_17);
  and and_2 (and_2_out, main_3_o, out_17);
  Adder_main main_1 (.in_1(in_1), .in_2(in_7), .Cy(main_3_cyout), .O(out_17), .CyOut(main_1_cyout));
  Adder_main main_2 (.in_1(Detector), .in_2(main_3_o), .Cy(main_4_cy), .O(out_15), .CyOut(main_2_cyout));
  Adder_main main_3 (.in_1(in_3), .in_2(in_9), .Cy(main_5_cyout), .O(main_3_o), .CyOut(main_3_cyout));
  HalfAdder_main main_4 (.A(Detector), .B(main_5_o), .O(out_16), .Cy(main_4_cy));
  Adder_main main_5 (.in_1(in_4), .in_2(in_10), .Cy(xor_1_out), .O(main_5_o), .CyOut(main_5_cyout));
  or or_2 (Detector_2, main_6_cyout, and_4_out, and_3_out);
  xor xor_1 (xor_1_out, main_7_cyout, main_6_cyout);
  and and_3 (and_3_out, main_10_o, out_20);
  and and_4 (and_4_out, main_8_o, out_20);
  Adder_main main_6 (.in_1(in_5), .in_2(in_11), .Cy(main_8_cyout), .O(out_20), .CyOut(main_6_cyout));
  Adder_main main_7 (.in_1(Detector_2), .in_2(main_8_o), .Cy(main_9_cy), .O(out_13), .CyOut(main_7_cyout));
  Adder_main main_8 (.in_1(in_6), .in_2(in_12), .Cy(main_10_cy), .O(main_8_o), .CyOut(main_8_cyout));
  HalfAdder_main main_9 (.A(Detector_2), .B(main_10_o), .O(out_14), .Cy(main_9_cy));
  HalfAdder_main main_10 (.A(in_2), .B(in_8), .O(main_10_o), .Cy(main_10_cy));
endmodule
