// Logisim project 1.1.circ as structural Verilog: 1 circuit, main circuit main
module main (
  input  X
);

  wire A_q, A_qn, and_1_out, and_2_out, and_3_out, and_4_out, and_5_out, B_q, C_q, C_qn, clock_1_out,
       not_1_out, or_1_out, or_2_out;

  Clock clock_1 (.out(clock_1_out));
  not not_1 (not_1_out, X);
  and and_1 (and_1_out, A_qn, not_1_out);
  and and_2 (and_2_out, A_qn, B_q);
  and and_3 (and_3_out, A_qn, X);
  or or_1 (or_1_out, A_q, and_1_out);
  S_R_Flip_Flop B (.S(and_5_out), .clk(clock_1_out), .R(or_2_out), .Q(B_q));  // open: Qn, preset, reset, en
  or or_2 (or_2_out, and_4_out, A_q);
  S_R_Flip_Flop A (.S(and_2_out), .clk(clock_1_out), .R(A_q), .Q(A_q), .Qn(A_qn));  // open: preset, reset, en
  and and_4 (and_4_out, A_qn, C_qn);
  and and_5 (and_5_out, A_qn, C_q);
  S_R_Flip_Flop C (.S(and_3_out), .clk(clock_1_out), .R(or_1_out), .Q(C_q), .Qn(C_qn));  // open: preset, reset, en
endmodule
