// Logisim project 1.7-RS-D.circ as structural Verilog: 1 circuit, main circuit main
module main (
  input  in_1
);

  wire clock_1_out, not_1_out;

  Clock clock_1 (.out(clock_1_out));
  not not_1 (not_1_out, in_1);
  S_R_Flip_Flop s_r_ff_1 (.S(in_1), .clk(clock_1_out), .R(not_1_out));  // open: Q, Qn, preset, reset, en
endmodule
