// Logisim project 3.5.circ as structural Verilog: 1 circuit, main circuit main
module main (
  input  Op1,
  input  Op2,
  input  Op3,
  input  RegSel,
  input  M1,
  input  M2,
  input  M3
);

  wire and_1_out, and_3_out, and_4_out, and_5_out, and_6_out, and_7_out, and_8_out, and_9_out, clock_1_out,
       not_1_out, not_2_out, not_3_out, not_4_out, not_5_out, not_6_out, not_7_out, not_8_out, not_9_out,
       not_10_out, undriven, undriven_2, undriven_3;

  not not_1 (not_1_out, RegSel);
  // NOT_Gate not_2 has open pins: in=open, out=not_2_out
  not not_3 (not_3_out, Op1);
  not not_4 (not_4_out, Op2);
  // NOT_Gate not_5 has open pins: in=open, out=not_5_out
  not not_6 (not_6_out, Op3);
  and and_1 (and_1_out, not_6_out, not_4_out, not_3_out);
  // AND_Gate and_2 has open pins: in0=not_5_out, in1=not_2_out, in2=not_7_out, out=open
  and and_3 (and_3_out, and_1_out, not_1_out);
  // NOT_Gate not_7 has open pins: in=open, out=not_7_out
  Clock clock_1 (.out(clock_1_out));
  J_K_Flip_Flop B1 ();  // open: J, clk, K, Q, Qn, preset, en, reset
  J_K_Flip_Flop B2 ();  // open: J, clk, K, Q, Qn, preset, en, reset
  J_K_Flip_Flop B3 ();  // open: J, clk, K, Q, Qn, preset, en, reset
  and and_4 (and_4_out, undriven_2, undriven_3);
  not not_8 (not_8_out, undriven_3);
  and and_5 (and_5_out, not_8_out, undriven_2);
  and and_6 (and_6_out, undriven_2, undriven);
  not not_9 (not_9_out, undriven);
  and and_7 (and_7_out, not_9_out, undriven_2);
  and and_8 (and_8_out, undriven_2, M3);
  not not_10 (not_10_out, M3);
  and and_9 (and_9_out, not_10_out, undriven_2);
  J_K_Flip_Flop A1 (.J(and_4_out), .clk(clock_1_out), .K(and_5_out));  // open: Q, Qn, preset, en, reset
  J_K_Flip_Flop A2 (.J(and_6_out), .clk(clock_1_out), .K(and_7_out));  // open: Q, Qn, preset, en, reset
  J_K_Flip_Flop A3 (.J(and_8_out), .clk(clock_1_out), .K(and_9_out));  // open: Q, Qn, preset, en, reset

  // Notes on the sheet:
  //   RegSel decide el registro con el cual hacer las cargas
endmodule
